# Fritzing sketch Alarm_System (saved by Fritzing 0.9.3b)
breadboards: 1

parts:
  Part1 = Arduino Uno (Rev3) - ICSP
  J1 = Piezo Speaker
  LED1 = smd LED [color="Red (633nm)" package="1206 [SMD]"]
  LED2 = smd LED [color="Orange (620nm)" package="1206 [SMD]"]
  LED3 = smd LED [color="Blue (525nm)" package="1206 [SMD]"]
  LED4 = smd LED [color="Yellow (592nm)" package="1206 [SMD]"]
  LED5 = smd LED [color="Green (555nm)" package="1206 [SMD]"]
  LED6 = smd LED [color="Blue (430nm)" package="1206 [SMD]"]
  R1 = Resistor [tolerance=±5% resistance=330 package=THT]
  R2 = Resistor [tolerance=±5% resistance=330 package=THT]
  R3 = Resistor [tolerance=±5% resistance=330 package=THT]
  R4 = Resistor [tolerance=±5% resistance=330 package=THT]
  R5 = Resistor [tolerance=±5% resistance=330 package=THT]
  R6 = Resistor [tolerance=±5% resistance=330 package=THT]
  S1 = Pushbutton [package="[SMD]"]
  R7 = Resistor [tolerance=±5% resistance=1k package=THT]
  HC-SR04_Sensor_1 = HC-SR04 Ultrasonic Distance Sensor

nets:
  N1: Part1.ICSP_MISO, Part1.D12/MISO, HC-SR04_Sensor_1.ECHO
  5V: Part1.5V, S1.Pin_3, S1.Pin_4, HC-SR04_Sensor_1.VCC
  N2: Part1.ICSP_MOSI, Part1.D11_PWM/MOSI, HC-SR04_Sensor_1.TRIG
  GND: Part1.GND, J1.pin1, LED1.cathode, LED2.cathode, LED3.cathode, LED4.cathode, LED5.cathode, LED6.cathode, R7.Pin_1, HC-SR04_Sensor_1.GND
  N3: Part1.D9_PWM, J1.pin2
  N4: Part1.D10_PWM/SS, S1.Pin_1, S1.Pin_2, R7.Pin_0
  N5: Part1.D2, R1.Pin_1
  N6: Part1.D3_PWM, R2.Pin_1
  N7: Part1.D4, R3.Pin_1
  N8: Part1.D5_PWM, R4.Pin_1
  N9: Part1.D6_PWM, R5.Pin_1
  N10: Part1.D7, R6.Pin_1
  N11: LED1.anode, R1.Pin_0
  N12: LED2.anode, R2.Pin_0
  N13: LED3.anode, R4.Pin_0
  N14: LED4.anode, R3.Pin_0
  N15: LED5.anode, R5.Pin_0
  N16: LED6.anode, R6.Pin_0

// code stored in the sketch: deneme.ino
int buzzer = 9;
int buton = 10;
int ledler[] ={2,3,4,5,6,7};
int echo_pin = 12;
int trig_pin = 11;
long mesafe;
int alarm = 0;

void setup() {
Serial.begin(9600);
Serial.println("Sistem Aktiflestirildi...");
Serial.println(alarm);
pinMode(buzzer,OUTPUT);
pinMode(trig_pin,OUTPUT);
pinMode(echo_pin,INPUT);
for (int i = 0; i<6;i++)
{
  pinMode(ledler[i],OUTPUT);
}

}

void loop() {
if (alarm == 0 && digitalRead(buton))
{
  alarm_aktif();
  Serial.println(alarm);
  delay(1000);
  while (!digitalRead(buton))
  {
    mesafe = mesafeolcme();
    Serial.print("Mesafe: ");
    Serial.print(mesafe);
    Serial.println(" Cm");
    if (mesafe<20)
    {
      isikyak();
      digitalWrite(buzzer,HIGH);
      delay(100);
      digitalWrite(buzzer,LOW);
      delay(100);
    }
  }
  
}
else if(alarm == 1 && digitalRead(buton))
{
  delay(1000);
  alarm_pasif();
}
}

int mesafeolcme()
{
  long mesafe, sure;
  digitalWrite(trig_pin, LOW);
  delayMicroseconds(2);
  digitalWrite(trig_pin, HIGH);
  delayMicroseconds(10);
  digitalWrite(trig_pin, LOW);
  sure = pulseIn(echo_pin, HIGH);
  mesafe = (sure/2)/29.154;
  return mesafe;
}

void alarm_aktif()
{
  alarm = 1; 
  Serial.println("Alarm Aktiflestiriliyor...");
  for (int i = 0; i<10;i++)
  {
    digitalWrite(ledler[0],HIGH);
    delay(100);
    digitalWrite(ledler[0],LOW);
    delay(100);
  }
  digitalWrite(ledler[0],HIGH);
  digitalWrite(ledler[5],LOW);
  Serial.println("Alarm Aktiflestirildi...");
}

void alarm_pasif()
{
  alarm = 0; 
  Serial.println("Alarm Pasiflestiriliyor...");
  for (int i = 0; i<10;i++)
  {
    digitalWrite(ledler[5],HIGH);
    delay(100);
    digitalWrite(ledler[5],LOW);
    delay(100);
  }
  digitalWrite(ledler[5],HIGH);
  digitalWrite(ledler[0],LOW);
  Serial.println("Alarm Pasiflestirildi...");
}

void isikyak()
{
  for (int i = 1; i<5; i++)
  {
    digitalWrite(ledler[i], HIGH);
  }
  delay(100);
  for (int i = 1; i<5; i++)
  {
    digitalWrite(ledler[i], LOW);
  }
  delay(100);
}
